# Fritzing sketch BMP085 (saved by Fritzing 0.7.4b)
breadboards: 1

parts:
  BeagleBone1 = beaglebone-a5
  Composants1 = Barometric Pressure Sensor - BMP085 Breakout

nets:
  N1: BeagleBone1.connectorp9-1, Composants1.GND
  N2: BeagleBone1.connectorp9-5, Composants1.VCC
  N3: BeagleBone1.connectorp9-19, Composants1.SCL
  N4: BeagleBone1.connectorp9-20, Composants1.SDA

notes:
  P9_19 : I2C3-SCL
  P9_20 : I2C3-SDA
