# Fritzing sketch DS18B20 (saved by Fritzing 0.7.4b)
breadboards: 1

parts:
  BeagleBone1 = beaglebone-a5
  T1 = LM35 Temperature Sensor [package="TO92 [THT]"]

nets:
  N1: BeagleBone1.connectorp8-2, T1.+Vs
  N2: BeagleBone1.connectorp8-6, T1.Vout
  N3: BeagleBone1.connectorp9-5, T1.GND

notes:
  P8_2 : GND
  P8_6 : 1-wire
  P9_5 : VDD_5V
