# Fritzing sketch TMP36 (saved by Fritzing 0.7.4b)
breadboards: 1

parts:
  BeagleBone1 = beaglebone-a5
  T1 = LM35 Temperature Sensor [package="TO92 [THT]"]

nets:
  N1: BeagleBone1.connectorp9-5, T1.+Vs
  N2: BeagleBone1.connectorp9-33, T1.Vout

notes:
  P9_1 : GND
  P9_33 : AIN4
  P9_5 : VDD_5V
