# Fritzing sketch gpio-led (saved by Fritzing 0.7.4b)
breadboards: 1

parts:
  BeagleBone1 = beaglebone-a5
  Q1 = NPN-Transistor [package="TO92 [THT]"]
  R1 = Resistor [tolerance=±5% resistance=220 package=THT]
  R2 = Resistor [tolerance=±5% resistance=220 package=THT]
  LED1 = LED - 5mm [color="Red (633nm)" package="5 mm [THT]"]

nets:
  N1: BeagleBone1.connectorp9-5, LED1.anode
  N2: BeagleBone1.connectorp9-45, Q1.C
  N3: Q1.E, R1.Pin_0
  N4: Q1.B, R2.Pin_1
  N5: R1.Pin_1, LED1.cathode
